// Digital circuit tom-1.dig as structural Verilog
module tom_1 (
  input  clk,
  input  in_4,
  input  in_5,
  output pulse,
  output clk_2
);

  wire and_1_out, and_2_out, and_3_out, and_4_out, and_5_out, and_6_out, and_7_out, decoder_1_out_0,
       decoder_1_out_1, decoder_1_out_2, decoder_1_out_3, driver_1_out, nclk, not_2_out, not_3_out,
       not_4_out, not_5_out, not_6_out, not_7_out, npulse, nreset, nTOS_eq__eq_0_nis0, xor_1_out;
  wire [1:0] ROM_d_2;
  wire [7:0] D_REGISTER_q, driverinvsel_1_out, driverinvsel_1_out_2, NAND_out, NAND_out_2, ROM_d;
  wire [15:0] CTRL_2_p3, I_O_HI_p3, PROGRAM_COUNTER_pc, pulldown_1_out, TOS_HI_out;

  Reset reset_1 (.out(nreset));
  Break break_1 (.brk(driver_1_out));
  assign driver_1_out = in_5 ? npulse : 1'bz;  // Driver driver_1
  not not_1 (npulse, clk);
  LED led_1 (.in(npulse));
  // Probe on npulse
  LED led_2 (.in(clk));
  D_FF d_ff_1 (.D(clk_2), .C(npulse), .Q(nclk), .nQ(clk_2));
  LED led_3 (.in(nclk));
  LED led_4 (.in(clk_2));
  Decoder #(.Selector_Bits(2)) decoder_1 (
    .sel(ROM_d_2), .out_0(decoder_1_out_0), .out_1(decoder_1_out_1), .out_2(decoder_1_out_2),
    .out_3(decoder_1_out_3));
  and and_1 (and_1_out, ROM_d[4], clk);
  tom_1_is0 nTOS_eq__eq_0 (.\input ({driverinvsel_1_out_2, driverinvsel_1_out}), .nis0(nTOS_eq__eq_0_nis0));
  // Probe tos_bus on {NAND_out_2, NAND_out}
  not not_2 (not_2_out, nTOS_eq__eq_0_nis0);
  not not_3 (not_3_out, ROM_d[1]);
  and and_2 (and_2_out, ~ROM_d[1], and_1_out);  // And
  and and_3 (and_3_out, ~not_3_out, and_1_out);  // And
  Break BREAK_2 (.brk(ROM_d[7]));
  tom_1_273 TOS_LO (.nCLR(nreset), .DATA(NAND_out), .CLK(nclk), .OUT(TOS_HI_out[7:0]));
  tom_1_273 TOS_HI (.nCLR(nreset), .DATA(NAND_out_2), .CLK(nclk), .OUT(TOS_HI_out[15:8]));
  // Probe CCK on and_1_out
  and and_4 (and_4_out, not_2_out, clk, ROM_d[7]);
  tom_1_d_r D_REGISTER (
    .nENP(1'b0), .nCCLR(nreset), .RCK(clk), .R_nC(1'b0), .nG(ROM_d[1]), .nLOAD(1'b1), .nENT(1'b0),
    .U_nD(ROM_d[2]), .D({8{1'b0}}), .CCK(and_2_out), .Q(D_REGISTER_q));
  tom_1_d_r R_REGISTER (
    .nENP(1'b0), .nCCLR(nreset), .RCK(clk), .R_nC(1'b0), .nG(not_3_out), .nLOAD(1'b1), .nENT(1'b0),
    .U_nD(ROM_d[2]), .D({8{1'b0}}), .CCK(and_3_out), .Q(D_REGISTER_q));
  // Probe dr on D_REGISTER_q
  xor xor_1 (xor_1_out, nreset, and_4_out);
  assign {driverinvsel_1_out_2, driverinvsel_1_out} = ~ROM_d[0] ? TOS_HI_out : 16'bz;  // DriverInvSel driverinvsel_1
  SixteenSeg sixteenseg_1 (.led({driverinvsel_1_out_2, driverinvsel_1_out}), .dp(1'b0));
  // Probe TOS on {driverinvsel_1_out_2, driverinvsel_1_out}
  tom_1_pc PROGRAM_COUNTER (.clk(npulse), .\input (pulldown_1_out), .nLOAD(xor_1_out), .pc(PROGRAM_COUNTER_pc));
  not not_4 (not_4_out, decoder_1_out_1);
  and and_5 (and_5_out, not_4_out, ROM_d[3]);
  // tom_1_ctrl CTRL: pin names not known; wires that end beside it: npulse, PROGRAM_COUNTER_pc[7:0], CTRL_2_p3[7:0]
  // tom_1_ctrl CTRL_2: pin names not known; wires that end beside it: npulse, PROGRAM_COUNTER_pc[15:8], CTRL_2_p3[15:8]
  not not_5 (not_5_out, ROM_d[3]);
  not not_6 (not_6_out, and_5_out);
  // Probe ~d/r on ROM_d[1]
  not not_7 (not_7_out, decoder_1_out_1);
  and and_6 (and_6_out, decoder_1_out_1, not_5_out);
  and and_7 (and_7_out, decoder_1_out_1, ROM_d[3]);
  // tom_1_io I_O_LO: pin names not known; wires that end beside it: driverinvsel_1_out, not_6_out, I_O_HI_p3[7:0]
  // tom_1_io I_O_HI: pin names not known; wires that end beside it: driverinvsel_1_out_2, not_6_out, I_O_HI_p3[15:8]
  // Probe stack addr on {ROM_d[1], D_REGISTER_q}
  PullDown #(.Bits(16)) pulldown_1 (.out(pulldown_1_out));
  // Probe PC on CTRL_2_p3
  RAMSinglePortSel #(.AddrBits(9), .Bits(16)) STACK (
    .A({ROM_d[1], D_REGISTER_q}), .CS(1'b1), .WE(ROM_d[3]), .OE(not_7_out), .D(I_O_HI_p3));
  RAMSinglePortSel #(.AddrBits(16), .Bits(16)) RAM (
    .A({driverinvsel_1_out_2, driverinvsel_1_out}), .CS(1'b1), .WE(and_6_out), .OE(and_7_out), .D(I_O_HI_p3));
  EEPROM #(.AddrBits(16), .isProgramMemory("true"), .Bits(16)) ROM (
    .A(CTRL_2_p3), .CS(1'b1), .WE(1'b0), .OE(nreset), .D({ROM_d[7], ROM_d_2, ROM_d[4:0], pulldown_1_out[7:0]}));
  // Probe ROM on pulldown_1_out
  // Probe stack_bus on I_O_HI_p3
  // tom_1_ctrl CTRL_3: pin names not known; wires that end beside it: nclk, pulldown_1_out[7:0], pulldown_1_out[15:8]
  // Probe CTRL on {ROM_d[7], ROM_d_2, ROM_d[4:0]}
  tom_1_nand NAND (
    .A({driverinvsel_1_out_2, driverinvsel_1_out}), .B(I_O_HI_p3), .enable(decoder_1_out_3),
    .out({NAND_out_2, NAND_out}));
  // tom_1_add tom_1_add_1: pin names not known; wires that end beside it: {driverinvsel_1_out_2, driverinvsel_1_out}, I_O_HI_p3, decoder_1_out_2, {NAND_out_2, NAND_out}
  assign {NAND_out_2, NAND_out} = decoder_1_out_0 ? pulldown_1_out : 16'bz;  // Driver driver_2

  assign pulse = clk;

  // Other names for the same wires on the sheet: clk_t = clk_2

  // Notes on the sheet:
  //   clk: Hz: 3
  //   in_5: default 1
  //   Clock
  //   CTRLs needed until PC latching works
  //   contents of ROM (hex, n*v repeats v):
  //   0,100,1cca,cfe,1c00,c10,3000,4100,1c00,c10,3400,5100,1000,4100,1c00,c00,1000,8000,
  //   1c00,c01,1000,8000
  //   This is implicity two ICs
endmodule
